// Digital circuit Lab02.dig as structural Verilog
module Lab02 (
  input  B,
  input  C,
  input  A,
  input  D,
  output Fa,
  output Fb,
  output Fc,
  output Fd,
  output Fe,
  output Fg,
  output Ff
);

  wire Ai, and_1_out, and_2_out, and_3_out, and_4_out, and_5_out, Ci, Di, Do;

  // Not not_1 is placed but not wired
  not not_2 (Ci, C);
  not not_3 (Di, Do);
  and and_1 (and_1_out, A, B, Ci);
  and and_2 (and_2_out, Ai, B, Do);
  and and_3 (and_3_out, B, Di);
  and and_4 (and_4_out, Ai, C);
  and and_5 (and_5_out, B, C);
  not not_4 (Ai, A);
  or or_1 (Fa, and_1_out, and_2_out, and_3_out, and_4_out, and_5_out);
  Seven_Seg seven_seg_1 (.dp(1'b0));  // open: a, b, c, d, e, f, g

  assign D = C;

  // Other names for the same wires on the sheet: Ao = A; Bi = B; Bo = B; Co = C
endmodule
